# Fritzing sketch max7291 (saved by Fritzing 0.9.3b)

parts:
  Componente1 = LED Matrix - Serial Interface - Red/Green/Blue
  Componente2 = Arduino Uno (Rev3)

nets:
  GND: Componente1.GND, Componente2.GND
  N1: Componente1.MOSI, Componente2.D12/MISO
  N2: Componente1.CS, Componente2.D11_PWM/MOSI
  N3: Componente1.SCK, Componente2.D10_PWM/SS
  VCC: Componente1.VCC, Componente2.5V
